// Logisim project Guess The Number XTREME.circ as structural Verilog: 11 circuits, main circuit main
module main (
  input  in_1,
  input  in_2,
  input  in_3,
  input  in_4,
  input  in_5,
  input  in_6,
  input  in_7,
  input  in_8
);

  wire ACERTOU, CHUTANDO_X, CHUTANDO_Y, CHUTAR, CLK_CRONO, cronometro_1_end, cronometro_2_end, d_ff_1_q,
       d_ff_2_q, flip_flop_t_1_q, flip_flop_t_2_q, or_1_out, or_2_out, RESET, SALVAR, START, SX, SY, TROCAR,
       tunnel, tunnel_t, tunnel_t_t, TURNO_A, TURNO_B, undriven, undriven_2, undriven_5, undriven_6,
       undriven_7, undriven_8, undriven_9;
  wire [3:0] decode_comp2_1_out_5, decode_comp2_2_out_5, DMA, DMB, DSA, DSB, MAGIC_X, MAGIC_Y, NUM_A, NUM_B,
       NX, NY, UMA, UMB, undriven_3, undriven_4, USA, USB, XCHUTE, YCHUTE;

  Button button_1 ();  // open: out
  Hex_Digit_Display hex_digit_display_1 (.value(DMA));  // open: dp
  Button button_2 ();  // open: out
  Hex_Digit_Display hex_digit_display_2 (.value(UMA));  // open: dp
  LED SA (.in(in_1));
  Hex_Digit_Display hex_digit_display_3 (.value(decode_comp2_1_out_5));  // open: dp
  decode_comp2 decode_comp2_1 (.A3(in_1), .A2(in_2), .A1(in_3), .A0(in_4), .out_6(NUM_A), .out_5(decode_comp2_1_out_5));
  Clock clock_1 (.out(CLK_CRONO));
  decode_coordenada decode_coordenada_1 (.Q(flip_flop_t_1_q), .X(CHUTANDO_X), .Y(CHUTANDO_Y));
  flip_flop_T flip_flop_t_1 (.D(TROCAR), .Q(flip_flop_t_1_q));  // open: Q_prime
  Button button_3 ();  // open: out
  Hex_Digit_Display hex_digit_display_4 (.value(DSA));  // open: dp
  Button button_4 ();  // open: out
  Hex_Digit_Display hex_digit_display_5 (.value(USA));  // open: dp
  LED JOGA_A (.in(TURNO_A));
  LED X (.in(CHUTANDO_X));
  chuteXY chutexy_1 (
    .CHUTEA(NUM_A), .CLK(SALVAR), .SELETOR_COO(flip_flop_t_1_q), .X(NX), .Y(NY),
    .SELETOR_JOG(flip_flop_t_2_q), .CHUTEB(NUM_B), .XS(SX), .YS(SY), .XCOMP2(XCHUTE), .YCOMP2(YCHUTE));
  decode_jogador decode_jogador_1 (.Q(flip_flop_t_2_q), .J_A(TURNO_A), .J_B(TURNO_B));
  flip_flop_T flip_flop_t_2 (.D(CHUTAR), .Q(flip_flop_t_2_q));  // open: Q_prime
  Button u_START (.out(START));
  LED A_VENCEU ();  // open: in
  LED \MODO_EDIÇÃO  ();  // open: in
  LED MAIOR (.in(tunnel_t_t));
  Button u_TROCAR (.out(TROCAR));
  LED u_SX (.in(SX));
  Hex_Digit_Display hex_digit_display_6 (.value(NX));  // open: dp
  LED FIM_DE_JOGO ();  // open: in
  LED EMPATE ();  // open: in
  LED u_ACERTOU (.in(ACERTOU));
  LED IGUAL (.in(tunnel_t));
  LED MENOR (.in(tunnel));
  LED u_SY (.in(SY));
  Button u_SALVAR (.out(SALVAR));
  LED B_VENCEU ();  // open: in
  Button CONFIGURAR ();  // open: out
  Button u_RESET (.out(RESET));
  Button u_CHUTAR (.out(CHUTAR));
  Hex_Digit_Display hex_digit_display_7 (.value(NY));  // open: dp
  comparador comparador_1 (
    .CHUTE_X(XCHUTE), .CHUTE_Y(YCHUTE), .X(MAGIC_X), .Y(MAGIC_Y), .CLK(CHUTAR), .IGUAL(ACERTOU),
    .SOMA_MAIOR(tunnel_t_t), .SOMA_IGUAL(tunnel_t), .SOMA_MENOR(tunnel));
  coordenadas coordenadas_1 (.RESET(START), .X(MAGIC_X), .Y(MAGIC_Y));
  LED Y (.in(CHUTANDO_Y));
  Button button_5 ();  // open: out
  Button button_6 ();  // open: out
  Hex_Digit_Display hex_digit_display_8 (.value(DMB));  // open: dp
  Hex_Digit_Display hex_digit_display_9 (.value(UMB));  // open: dp
  LED JOGA_B (.in(TURNO_B));
  Button button_7 ();  // open: out
  Hex_Digit_Display hex_digit_display_10 (.value(DSB));  // open: dp
  LED SB (.in(in_5));
  Hex_Digit_Display hex_digit_display_11 (.value(decode_comp2_2_out_5));  // open: dp
  decode_comp2 decode_comp2_2 (.A3(in_5), .A2(in_6), .A1(in_7), .A0(in_8), .out_6(NUM_B), .out_5(decode_comp2_2_out_5));
  Button button_8 ();  // open: out
  Hex_Digit_Display hex_digit_display_12 (.value(USB));  // open: dp
  Cronometro cronometro_1 (
    .CLK(CLK_CRONO), .PAUSE(or_1_out), .CLEAR(undriven), .END(cronometro_1_end), .DM(DMA), .UM(UMA),
    .DS(DSA), .US(USA), .IDM(undriven_3[3]), .IUM(undriven_3[2]), .IDS(undriven_3[1]), .IUS(undriven_3[0]),
    .MODE(undriven_5));
  or or_1 (or_1_out, d_ff_1_q, undriven_7);
  Cronometro cronometro_2 (
    .CLK(CLK_CRONO), .PAUSE(or_2_out), .CLEAR(undriven_2), .END(cronometro_2_end), .DM(DMB), .UM(UMB),
    .DS(DSB), .US(USB), .IDM(undriven_4[3]), .IUM(undriven_4[2]), .IDS(undriven_4[1]), .IUS(undriven_4[0]),
    .MODE(undriven_6));
  buf or_2 (or_2_out, d_ff_2_q);  // OR_Gate
  D_Flip_Flop d_ff_1 (.Q(d_ff_1_q), .preset(cronometro_1_end), .reset(undriven_8));  // open: clk, D, Qn, en
  D_Flip_Flop d_ff_2 (.Q(d_ff_2_q), .preset(cronometro_2_end), .reset(undriven_9));  // open: clk, D, Qn, en
endmodule

module Cronometro (
  input  CLK,
  input  PAUSE,
  input  CLEAR,
  input  IDM,
  input  IUM,
  input  IDS,
  input  IUS,
  input  MODE,
  output END,
  output [3:0] DM,
  output [3:0] UM,
  output [3:0] DS,
  output [3:0] US
);

  wire and_1_out, and_2_out, and_3_out, and_4_out, and_5_out, and_6_out, and_7_out, and_8_out, and_9_out,
       and_10_out, and_11_out, comparator_1_eq, comparator_2_eq, comparator_3_eq, comparator_4_eq,
       decsm_2_vai1, or_1_out, or_2_out, or_3_out, unitsm_1_vai1, unitsm_2_vai1;
  wire [3:0] adder_1_out, register_1_q, register_2_q, register_3_q, register_4_q, subtractor_1_out,
       subtractor_2_out, subtractor_3_out;

  and and_1 (and_1_out, PAUSE, ~MODE);  // AND_Gate
  Register #(.width(4)) register_1 (.D(DM), .Q(register_1_q), .clk(and_2_out), .clr(CLEAR));  // open: en
  and and_2 (and_2_out, CLK, ~and_1_out);  // AND_Gate
  decSM decsm_1 (
    .A3(subtractor_1_out[3]), .A2(subtractor_1_out[2]), .A1(subtractor_1_out[1]), .A0(subtractor_1_out[0]),
    .S3(DM[3]), .S2(DM[2]), .S1(DM[1]), .S0(DM[0]));  // open: VAI1
  Subtractor #(.width(4)) subtractor_1 (
    .a(register_1_q), .b(4'b0000), .out(subtractor_1_out), .bin(or_1_out));  // open: bout
  and and_3 (and_3_out, MODE, IDM);
  and and_4 (and_4_out, unitsm_1_vai1, ~MODE);  // AND_Gate
  or or_1 (or_1_out, and_4_out, and_3_out);
  unitSM unitsm_1 (
    .A3(subtractor_2_out[3]), .A2(subtractor_2_out[2]), .A1(subtractor_2_out[1]), .A0(subtractor_2_out[0]),
    .S3(UM[3]), .S2(UM[2]), .S1(UM[1]), .S0(UM[0]), .VAI1(unitsm_1_vai1));
  Register #(.width(4)) register_2 (.D(UM), .Q(register_2_q), .clk(and_2_out), .clr(CLEAR));  // open: en
  and and_5 (and_5_out, decsm_2_vai1, ~MODE);  // AND_Gate
  or or_2 (or_2_out, and_5_out, and_6_out);
  Subtractor #(.width(4)) subtractor_2 (
    .a(register_2_q), .b(4'b0000), .out(subtractor_2_out), .bin(or_2_out));  // open: bout
  and and_6 (and_6_out, MODE, IUM);
  Comparator #(.width(4)) comparator_1 (.a(register_1_q), .b(4'b0000), .eq(comparator_1_eq));  // open: gt, lt
  Comparator #(.width(4)) comparator_2 (.a(register_2_q), .b(4'b0000), .eq(comparator_2_eq));  // open: gt, lt
  Comparator #(.width(4)) comparator_3 (.a(register_3_q), .b(4'b0000), .eq(comparator_3_eq));  // open: gt, lt
  Comparator #(.width(4)) comparator_4 (.a(register_4_q), .b(4'b0000), .eq(comparator_4_eq));  // open: gt, lt
  and and_7 (and_7_out, comparator_1_eq, comparator_2_eq, comparator_3_eq, comparator_4_eq);
  decSM decsm_2 (
    .A3(subtractor_3_out[3]), .A2(subtractor_3_out[2]), .A1(subtractor_3_out[1]), .A0(subtractor_3_out[0]),
    .S3(DS[3]), .S2(DS[2]), .S1(DS[1]), .S0(DS[0]), .VAI1(decsm_2_vai1));
  Register #(.width(4)) register_3 (.D(DS), .Q(register_3_q), .clk(and_2_out), .clr(CLEAR));  // open: en
  and and_8 (and_8_out, MODE, IDS);
  D_Flip_Flop d_ff_1 (.Q(END), .preset(and_7_out));  // open: clk, D, Qn, en, reset
  Subtractor #(.width(4)) subtractor_3 (
    .a(register_3_q), .b(4'b0000), .out(subtractor_3_out), .bin(or_3_out));  // open: bout
  and and_9 (and_9_out, unitsm_2_vai1, ~MODE);  // AND_Gate
  or or_3 (or_3_out, and_9_out, and_8_out);
  Register #(.width(4)) register_4 (.D(US), .Q(register_4_q), .clk(and_2_out), .clr(CLEAR));  // open: en
  unitSM unitsm_2 (
    .A3(adder_1_out[3]), .A2(adder_1_out[2]), .A1(adder_1_out[1]), .A0(adder_1_out[0]), .S3(US[3]),
    .S2(US[2]), .S1(US[1]), .S0(US[0]), .VAI1(unitsm_2_vai1));
  Adder #(.width(4)) adder_1 (.a(4'b1111), .b(register_4_q), .out(adder_1_out), .cin(and_10_out));  // open: cout
  and and_10 (and_10_out, MODE, ~and_11_out);  // AND_Gate
  and and_11 (and_11_out, MODE, IUS);
endmodule

module unitSM (
  input  A3,
  input  A2,
  input  A1,
  input  A0,
  output S3,
  output S2,
  output S1,
  output S0,
  output VAI1
);

  wire and_1_out, and_2_out, and_3_out, and_4_out, and_5_out, and_6_out, and_7_out, and_8_out, and_9_out,
       and_10_out, and_11_out, not_1_out, not_2_out, not_3_out, not_4_out, not_5_out, not_6_out, not_7_out,
       not_8_out;

  not not_1 (not_1_out, A3);
  not not_2 (not_2_out, A0);
  not not_3 (not_3_out, A3);
  not not_4 (not_4_out, A2);
  not not_5 (not_5_out, A0);
  not not_6 (not_6_out, A3);
  not not_7 (not_7_out, A2);
  not not_8 (not_8_out, A0);
  and and_1 (and_1_out, A3, A1);
  and and_2 (and_2_out, A3, A2);
  and and_3 (and_3_out, not_1_out, A2);
  or or_1 (S2, and_3_out, and_4_out);
  and and_4 (and_4_out, A2, not_2_out);
  and and_5 (and_5_out, not_3_out, A1);
  and and_6 (and_6_out, not_4_out, A1);
  or or_2 (S1, and_5_out, and_6_out, and_7_out);
  and and_7 (and_7_out, A1, not_5_out);
  and and_8 (and_8_out, not_6_out, A0);
  and and_9 (and_9_out, not_7_out, A0);
  and and_10 (and_10_out, A1, A0);
  and and_11 (and_11_out, A3, A2, not_8_out);
  or or_3 (VAI1, and_1_out, and_2_out);
  or or_4 (S0, and_8_out, and_9_out, and_10_out, and_11_out);

  assign S3 = A3;
endmodule

module decSM (
  input  A3,
  input  A2,
  input  A1,
  input  A0,
  output S3,
  output S2,
  output S1,
  output S0,
  output VAI1
);

  wire and_1_out, and_2_out, and_3_out, and_4_out, and_5_out, not_1_out, not_2_out, not_3_out, not_4_out;

  not not_1 (not_1_out, A3);
  not not_2 (not_2_out, A2);
  not not_3 (not_3_out, A0);
  not not_4 (not_4_out, A3);
  and and_1 (and_1_out, not_1_out, A1);
  or or_1 (S1, and_1_out, and_2_out, and_3_out);
  and and_2 (and_2_out, not_2_out, A1);
  and and_3 (and_3_out, A1, not_3_out);
  and and_4 (and_4_out, not_4_out, A0);
  or or_2 (S0, and_4_out, and_5_out);
  and and_5 (and_5_out, A2, A1, A0);

  assign S2 = A2;
  assign S3 = 1'b0;
  assign VAI1 = A3;
endmodule

module comparador (
  input  [3:0] CHUTE_X,
  input  [3:0] CHUTE_Y,
  input  [3:0] X,
  input  [3:0] Y,
  input  CLK,
  output IGUAL,
  output SOMA_MAIOR,
  output SOMA_IGUAL,
  output SOMA_MENOR
);

  wire and_1_out, comparator_1_eq, comparator_2_eq, comparator_3_eq, comparator_3_gt, comparator_3_lt;
  wire [3:0] adder_1_out, adder_2_out;

  Comparator #(.width(4)) comparator_1 (.a(CHUTE_X), .b(X), .eq(comparator_1_eq));  // open: gt, lt
  Comparator #(.width(4)) comparator_2 (.a(CHUTE_Y), .b(Y), .eq(comparator_2_eq));  // open: gt, lt
  Adder #(.width(4)) adder_1 (.a(CHUTE_X), .b(CHUTE_Y), .out(adder_1_out));  // open: cin, cout
  Adder #(.width(4)) adder_2 (.a(X), .b(Y), .out(adder_2_out));  // open: cin, cout
  and and_1 (and_1_out, comparator_1_eq, comparator_2_eq);
  Comparator #(.width(4)) comparator_3 (
    .a(adder_1_out), .b(adder_2_out), .gt(comparator_3_gt), .eq(comparator_3_eq), .lt(comparator_3_lt));
  D_Flip_Flop d_ff_1 (.clk(CLK), .D(and_1_out), .Q(IGUAL));  // open: Qn, preset, en, reset
  D_Flip_Flop d_ff_2 (.clk(CLK), .D(comparator_3_gt), .Q(SOMA_MAIOR));  // open: Qn, preset, en, reset
  D_Flip_Flop d_ff_3 (.clk(CLK), .D(comparator_3_eq), .Q(SOMA_IGUAL));  // open: Qn, preset, en, reset
  D_Flip_Flop d_ff_4 (.clk(CLK), .D(comparator_3_lt), .Q(SOMA_MENOR));  // open: Qn, preset, en, reset
endmodule

module flip_flop_T (
  input  D,
  output Q,
  output Q_prime
);

  wire and_1_out, and_2_out, and_3_out, d_ff_1_qn, not_1_out, not_2_out, not_3_out;

  not not_1 (not_1_out, D);
  not not_2 (not_2_out, not_1_out);
  not not_3 (not_3_out, not_2_out);
  and and_1 (and_1_out, not_3_out, D);
  and and_2 (and_2_out, Q, and_1_out);
  and and_3 (and_3_out, and_1_out, Q_prime);
  D_Flip_Flop d_ff_1 (.Qn(d_ff_1_qn), .preset(Q_prime));  // open: clk, D, Q, en, reset
  nor nor_1 (Q, and_2_out, d_ff_1_qn, Q_prime);
  nor nor_2 (Q_prime, Q, and_3_out);
endmodule

module coordenadas (
  input  RESET,
  output [3:0] X,
  output [3:0] Y
);

  wire and_1_out, not_1_out, not_2_out, not_3_out;

  not not_1 (not_1_out, RESET);
  not not_2 (not_2_out, not_3_out);
  not not_3 (not_3_out, not_1_out);
  and and_1 (and_1_out, not_2_out, RESET);
  Random #(.width(4)) random_1 (.clk(and_1_out), .out(X));  // open: next, clr
  Random #(.width(4), .seed(64)) random_2 (.clk(and_1_out), .out(Y));  // open: next, clr
endmodule

module chuteXY (
  input  [3:0] CHUTEA,
  input  [3:0] CHUTEB,
  input  CLK,
  input  SELETOR_COO,
  input  SELETOR_JOG,
  output XS,
  output [3:0] X,
  output YS,
  output [3:0] Y,
  output [3:0] XCOMP2,
  output [3:0] YCOMP2
);

  wire and_1_out, and_2_out, and_3_out, not_1_out, not_2_out, not_3_out;
  wire [3:0] multiplexer_1_out;

  Multiplexer #(.width(4)) multiplexer_1 (
    .in0(CHUTEA), .in1(CHUTEB), .out(multiplexer_1_out), .sel(SELETOR_JOG));  // open: en
  not not_1 (not_1_out, not_2_out);
  not not_2 (not_2_out, CLK);
  not not_3 (not_3_out, not_1_out);
  and and_1 (and_1_out, not_3_out, CLK);
  Register #(.width(4)) u_X (.D(multiplexer_1_out), .Q(XCOMP2), .clk(and_2_out));  // open: en, clr
  and and_2 (and_2_out, and_1_out, ~SELETOR_COO);  // AND_Gate
  Register #(.width(4)) u_Y (.D(multiplexer_1_out), .Q(YCOMP2), .clk(and_3_out));  // open: en, clr
  and and_3 (and_3_out, and_1_out, SELETOR_COO);
  decode_comp2 decode_comp2_1 (
    .A3(XCOMP2[3]), .A2(XCOMP2[2]), .A1(XCOMP2[1]), .A0(XCOMP2[0]), .out_5(X));  // open: out_6
  decode_comp2 decode_comp2_2 (
    .A3(YCOMP2[3]), .A2(YCOMP2[2]), .A1(YCOMP2[1]), .A0(YCOMP2[0]), .out_5(Y));  // open: out_6

  assign XS = XCOMP2[3];
  assign YS = YCOMP2[3];
endmodule

module decode_coordenada (
  input  Q,
  output X,
  output Y
);

  not not_1 (X, Q);

  assign Y = Q;
endmodule

module decode_jogador (
  input  Q,
  output J_A,
  output J_B
);

  not not_1 (J_A, Q);

  assign J_B = Q;
endmodule

module decode_comp2 (
  input  A3,
  input  A2,
  input  A1,
  input  A0,
  output [3:0] out_5,
  output [3:0] out_6
);

  wire and_2_out, and_3_out, and_4_out, and_5_out, and_6_out, and_7_out, and_8_out, not_1_out, not_2_out,
       not_3_out, not_4_out, not_5_out, not_6_out, not_7_out, not_8_out, not_9_out, not_10_out, not_11_out;

  not not_1 (not_1_out, A2);
  not not_2 (not_2_out, A1);
  not not_3 (not_3_out, A0);
  not not_4 (not_4_out, A3);
  not not_5 (not_5_out, A1);
  not not_6 (not_6_out, A0);
  not not_7 (not_7_out, A2);
  not not_8 (not_8_out, A2);
  not not_9 (not_9_out, A3);
  not not_10 (not_10_out, A0);
  not not_11 (not_11_out, A1);
  and and_1 (out_5[3], A3, not_1_out, not_2_out, not_3_out);
  and and_2 (and_2_out, not_4_out, A2);
  and and_3 (and_3_out, A2, not_5_out, not_6_out);
  and and_4 (and_4_out, A3, not_7_out, A0);
  and and_5 (and_5_out, A3, not_8_out, A1);
  and and_6 (and_6_out, not_9_out, A1);
  and and_7 (and_7_out, A1, not_10_out);
  and and_8 (and_8_out, A3, not_11_out, A0);
  or or_1 (out_5[2], and_2_out, and_3_out, and_4_out, and_5_out);
  or or_2 (out_5[1], and_6_out, and_7_out, and_8_out);

  assign out_5[0] = A0;
  assign out_6 = {A3, A2, A1, A0};
endmodule
